// Logisim project bitbit.circ as structural Verilog: 3 circuits, main circuit fulladder
module fulladder (
  input  carryin,
  input  b,
  input  a,
  output sum,
  output carryout
);

  wire and_1_out, and_2_out, xor_1_out;

  xor xor_1 (xor_1_out, b, a);
  and and_1 (and_1_out, b, a);
  and and_2 (and_2_out, b, xor_1_out);
  xor xor_2 (sum, b, xor_1_out);
  or or_1 (carryout, and_2_out, and_1_out);

  assign carryin = b;
endmodule

module main (
  input  in_1,
  input  in_2,
  input  in_3,
  input  in_4,
  input  in_5,
  input  in_6,
  input  in_7,
  input  in_8,
  input  in_9,
  input  in_10,
  input  in_11,
  input  in_12,
  input  in_13,
  input  in_14,
  input  in_15,
  input  in_16,
  output out_17,
  output out_18,
  output out_19,
  output out_20,
  output out_21,
  output out_22,
  output out_23,
  output out_24,
  output out_25
);

  wire fulladder_2_carryout, fulladder_3_carryout, fulladder_4_carryout, fulladder_5_carryout,
       fulladder_6_carryout, fulladder_7_carryout, halfadder_1_out_4;

  fulladder fulladder_1 (.carryin(fulladder_2_carryout), .b(in_2), .a(in_1), .sum(out_25), .carryout(out_24));
  fulladder fulladder_2 (
    .carryin(fulladder_3_carryout), .b(in_4), .a(in_3), .sum(out_17), .carryout(fulladder_2_carryout));
  fulladder fulladder_3 (
    .carryin(fulladder_4_carryout), .b(in_6), .a(in_5), .sum(out_18), .carryout(fulladder_3_carryout));
  fulladder fulladder_4 (
    .carryin(fulladder_5_carryout), .b(in_8), .a(in_7), .sum(out_19), .carryout(fulladder_4_carryout));
  fulladder fulladder_5 (
    .carryin(fulladder_6_carryout), .b(in_10), .a(in_9), .sum(out_20), .carryout(fulladder_5_carryout));
  fulladder fulladder_6 (
    .carryin(fulladder_7_carryout), .b(in_12), .a(in_11), .sum(out_21), .carryout(fulladder_6_carryout));
  fulladder fulladder_7 (
    .carryin(halfadder_1_out_4), .b(in_14), .a(in_13), .sum(out_22), .carryout(fulladder_7_carryout));
  halfadder halfadder_1 (.in_1(in_16), .in_2(in_15), .out_3(out_23), .out_4(halfadder_1_out_4));
endmodule

module halfadder (
  input  in_1,
  input  in_2,
  output out_3,
  output out_4
);

  xor xor_1 (out_3, in_1, in_2);
  and and_1 (out_4, in_1, in_2);
endmodule
