// Logisim project circuitcircuit.circ as structural Verilog: 3 circuits, main circuit halfadder
module halfadder (
  input  in_1,
  input  in_2,
  output out_3,
  output out_4
);

  xor xor_1 (out_3, in_1, in_2);
  and and_1 (out_4, in_1, in_2);
endmodule

module fulladder (
  input  carryin,
  input  a,
  input  b,
  output sum,
  output carryout
);

  wire and_1_out, and_2_out, xor_1_out;

  xor xor_1 (xor_1_out, a, b);
  and and_1 (and_1_out, a, b);
  xor xor_2 (sum, carryin, xor_1_out);
  and and_2 (and_2_out, carryin, xor_1_out);
  or or_1 (carryout, and_2_out, and_1_out);
endmodule

module main (
  input  in_1,
  input  in_2,
  input  in_3,
  input  in_4,
  input  in_5,
  input  in_6,
  input  in_7,
  input  in_8,
  input  in_9,
  input  in_10,
  input  in_11,
  input  in_12
);

  wire fulladder_2_carryout, fulladder_3_carryout, fulladder_4_carryout, fulladder_5_carryout,
       fulladder_6_carryout, fulladder_7_carryout, fulladder_8_carryout;

  fulladder fulladder_1 (.carryin(fulladder_2_carryout), .a(in_10), .b(in_9));  // open: sum, carryout
  fulladder fulladder_2 (
    .carryin(fulladder_3_carryout), .a(in_2), .b(in_1), .carryout(fulladder_2_carryout));  // open: sum
  fulladder fulladder_3 (
    .carryin(fulladder_4_carryout), .a(in_4), .b(in_3), .carryout(fulladder_3_carryout));  // open: sum
  fulladder fulladder_4 (
    .carryin(fulladder_5_carryout), .a(in_6), .b(in_5), .carryout(fulladder_4_carryout));  // open: sum
  fulladder fulladder_5 (
    .carryin(fulladder_6_carryout), .a(in_8), .b(in_7), .carryout(fulladder_5_carryout));  // open: sum
  fulladder fulladder_6 (.carryin(fulladder_7_carryout), .carryout(fulladder_6_carryout));  // open: a, b, sum
  fulladder fulladder_7 (.carryin(fulladder_8_carryout), .carryout(fulladder_7_carryout));  // open: a, b, sum
  fulladder fulladder_8 (.carryout(fulladder_8_carryout));  // open: carryin, a, b, sum
endmodule
