// Logisim project zz.circ as structural Verilog: 1 circuit, main circuit main
module main (
  input  in_1,
  input  in_2,
  input  in_3,
  output out_4
);

  wire nor_1_out, not_1_out, xor_1_out;

  not not_1 (not_1_out, in_1);
  nor nor_1 (nor_1_out, not_1_out, in_2);
  xor xor_1 (xor_1_out, in_1, in_3);
  nand nand_1 (out_4, nor_1_out, xor_1_out);
endmodule
